# Fritzing sketch House-io (saved by Fritzing 0.9.1b)
circuit board: 3.30845cm x 4.95284cm
perfboards: 1

parts:
  House_io = Spark Core (v1.0)
  Transmitter = mystery part, 3 pins [chip_label=Transmitter]
  Receiver = mystery part, 4 pins [chip_label=Receiver]
  NEOPIXEL = Neopixel Strip -- Black (30/m)
  DHT1 = DHT22 Humidity and Temperature Sensor
  Q1 = TRANSISTOR_NPN [package=to-92]
  D1 = LTE-302 [package=lte-302]
  R2 = Resistor [tolerance=±5% resistance=56 package=THT]
  R1 = Resistor [tolerance=±5% resistance=330 package=THT]

nets:
  N1: House_io.A0, Receiver.pin3
  GND: House_io.GND, Transmitter.pin3, Receiver.pin4, NEOPIXEL.GND, DHT1.GND, Q1.E
  N2: House_io.D0, R1.Pin_1
  N3: House_io.D1, Transmitter.pin1
  N4: House_io.D2, NEOPIXEL.Din
  N5: House_io.D3, DHT1.DATA
  3V3: House_io.3V3, Transmitter.pin2, Receiver.pin1, NEOPIXEL.+5V, DHT1.VDD, R2.Pin_0
  N6: Q1.B, R1.Pin_0
  N7: Q1.C, D1.C
  N8: D1.A, R2.Pin_1

custom parts:
  Neopixel Strip -- Black (30/m): These NeoPixel strips have 30 digitally-addressable pixel LEDs per meter and are very affordable and are only 12.5 mm wide, 10 mm if you remove the strip from the casing.

// code stored in the sketch: house-io.ino
/* IRrecord (Redux)
   by: Jim Lindblom
   SparkFun Electronics
   date: October 1, 2013

   This sketch uses Ken Shirriff's *awesome* IRremote library:
       https://github.com/shirriff/Arduino-IRremote
   It's a slightly modified version of the IRrecord example that
   comes with that library.

   This sketch uses the IR receiver diode to "record" an IR code.
   Then, when triggered via a button on pin 12, it will transmit
   that IR code out of an attached IR LED on pin 3.

   Hardware setup:
     * The output of an IR Receiver Diode (38 kHz demodulating
       version) should be connected to the Arduino's pin 11.
       * The IR Receiver diode should also be powered off the
         Arduino's 5V and GND rails.
     * The anode (+, longer leg) of an IR LED should be connected to pin 3 of 
       the Arduino. The cathode (-) should be connected to a 330
       Ohm resistor, which connects to ground.
     * A button should be connected to ground on one end, and pin
       12 of the Arduino on the other.

*/
#include <IRremote.h> // Include the IRremote library

/* Connect the output of the IR receiver diode to pin 11. */
int RECV_PIN = 11;
/* Initialize the irrecv part of the IRremote  library */
IRrecv irrecv(RECV_PIN);
decode_results results; // This will store our IR received codes

IRsend irsend; // Enables IR transmit on pin 3

/* Storage variables for the received IR code: */
unsigned int irLen = 0; // The length of the code
unsigned int irBuffer[RAWBUF]; // Storage for raw (UNKNOWN) codes
int codeType; // The type of code (NEC, SONY, UNKNOWN, etc.)
unsigned int codeValue; // The value of a known code
boolean codeReceived = false; // A boolean to keep track of if a code was received

const int buttonPin = 12; // Button pin. Pulled up. Triggered when connected to ground.

// setup() initializes serial and the Infrared receiver.
void setup()
{
  Serial.begin(9600);
  irrecv.enableIRIn(); // Start the receiver

  pinMode(buttonPin, INPUT_PULLUP);
}

// loop() checks for either a button press or a received IR code.
void loop()
{
  if (irrecv.decode(&results)) 
  {
    updateIRReceive(); // Sort out the received code
    codeReceived = true; // Enables code transmit on button press
    irrecv.resume(); // re-enable receive
  }

  // If the button is pressed, and we've received a code...
  if ((digitalRead(buttonPin) == LOW) && (codeReceived == true))
  {
    sendCode(); // Sends out our code. (See bottom of sketch).
    irrecv.enableIRIn(); // Re-enable receiver
    // We only want to be able to send the code once. Re-set
    // codeReceived to false:
    codeReceived = false;
  }
}

/* This function reads in the received IR data, and updates the
   following variables:
    * codeType -- How was the IR signal encoded? SONY, NEC, 
      UNKNOWN, etc.
    * irLen -- The length (number of marks and ticks) of an IR code.
    * Depending on the codeType, one of these two variables will
      be updated as well:
      * codeValue -- IF the codeType is a known type, this variable
        will contain the received code.
      * irBuffer -- If the codeType is UNKNOWN, this buffer will
        contain the format of the received code.

    This function borrows heavily from the IRrecord example code.
*/
void updateIRReceive()
{
  codeType = results.decode_type;
  irLen = results.rawlen;
  if (codeType == UNKNOWN)
  {
    irLen--;
    // We need to convert from ticks to microseconds
    for (int i = 1; i <= irLen; i++) 
    {
      if (i % 2) 
      {
        // Mark
        irBuffer[i-1] = results.rawbuf[i]*USECPERTICK - MARK_EXCESS;
        Serial.print(" m");
      } 
      else 
      {
        // Space
        irBuffer[i-1] = results.rawbuf[i]*USECPERTICK + MARK_EXCESS;
        Serial.print(" s");
      }
      Serial.print(irBuffer[i-1], DEC);
    }
    Serial.println();
  }
  else 
  {
    if (codeType == NEC) 
    {
      Serial.print("Received NEC: ");
      if (results.value == REPEAT) 
      {
        // Don't record a NEC repeat value as that's useless.
        Serial.println("repeat; ignoring.");
        return;
      }
    } 
    else if (codeType == SONY) 
    {
      Serial.print("Received SONY: ");
    } 
    else if (codeType == RC5) 
    {
      Serial.print("Received RC5: ");
    } 
    else if (codeType == RC6) 
    {
      Serial.print("Received RC6: ");
    } 
    else 
    {
      Serial.print("Unexpected codeType ");
      Serial.print(codeType, DEC);
      Serial.println("");
    }
    Serial.println(results.value, HEX);
    codeValue = results.value;
    irLen = results.bits;
  }
}


void sendCode()
{
  if (codeType == NEC) 
  {
    irsend.sendNEC(codeValue, irLen);
    Serial.print("Sent NEC ");
    Serial.println(codeValue, HEX);
  } 
  else if (codeType == SONY)
  {
    irsend.sendSony(codeValue, irLen);
    Serial.print("Sent Sony ");
    Serial.println(codeValue, HEX);
  } 
  else if (codeType == RC5 || codeType == RC6) 
  {
    // Put the toggle bit into the code to send
    codeValue = codeValue & ~(1 << (irLen - 1));
    if (codeType == RC5) 
    {
      Serial.print("Sent RC5 ");
      Serial.println(codeValue, HEX);
      irsend.sendRC5(codeValue, irLen);
    } 
    else 
    {
      irsend.sendRC6(codeValue, irLen);
      Serial.print("Sent RC6 ");
      Serial.println(codeValue, HEX);
    }
  } 
  else if (codeType == UNKNOWN /* i.e. raw */) 
  {
    // Assume 38 KHz
    irsend.sendRaw(irBuffer, irLen, 38);
    Serial.println("Sent raw");
  }
}
